// Logisim project micropressor.circ as structural Verilog
module main (
);

  wire button_1_out, clock_1_out, control_unit_1_aluorload, control_unit_1_aluormem,
       control_unit_1_aluorstore, control_unit_1_beqorbne, control_unit_1_branch, control_unit_1_memwrite,
       control_unit_1_regwrite, multiplexer_2_out, nor_1_out, or_1_out;
  wire [1:0] and_1_out;
  wire [2:0] control_unit_1_out_5;
  wire [3:0] multiplexer_3_out;
  wire [15:0] adder_1_out, adder_2_out, adder_3_out, alu_design_1_out_4, bit_extender_3_out,
       multiplexer_1_out, multiplexer_4_out, multiplexer_5_out, ram_1_data, register_1_q,
       register_bank_1_out_7, register_bank_1_out_8, rom_1_data, undriven, undriven_2;

  Multiplexer #(.select(2), .width(16), .enable("false")) multiplexer_1 (
    .in0(adder_1_out), .in1(adder_2_out), .in2(adder_3_out), .out(multiplexer_1_out), .sel(and_1_out));  // open: in3
  Clock clock_1 (.out(clock_1_out));
  Button button_1 (.out(button_1_out));
  Register #(.width(16)) register_1 (
    .D(multiplexer_1_out), .Q(register_1_q), .clk(clock_1_out), .clr(button_1_out));  // open: en
  and and_1 (and_1_out[0], multiplexer_2_out, control_unit_1_branch);
  Adder #(.width(16)) adder_1 (.a(register_1_q), .b(16'h1), .out(adder_1_out));  // open: cin, cout
  CONTROL_UNIT_weef control_unit_weef_1 ();
  Multiplexer #(.enable("false")) multiplexer_2 (
    .in0(or_1_out), .in1(nor_1_out), .out(multiplexer_2_out), .sel(control_unit_1_beqorbne));
  ROM #(.addrWidth(16), .dataWidth(16)) rom_1 (.addr(register_1_q), .data(rom_1_data));  // open: sel
  Adder #(.width(16)) adder_2 (.a(undriven), .b(adder_1_out), .out(adder_2_out));  // open: cin, cout
  Bit_Extender #(.in_width(16), .out_width(4), .\type ("sign")) bit_extender_1 (.in(undriven), .out(rom_1_data[3:0]));
  Adder #(.width(16)) adder_3 (.a(undriven_2), .b(register_1_q), .out(adder_3_out));  // open: cin, cout
  Bit_Extender #(.in_width(16), .out_width(12), .\type ("sign")) bit_extender_2 (
    .in(undriven_2), .out(rom_1_data[11:0]));
  CONTROL_UNIT control_unit_1 (
    .OPCODE_15(rom_1_data[12]), .OPCODE_14(rom_1_data[13]), .OPCODE_13(rom_1_data[14]),
    .OPCODE_12(rom_1_data[15]), .RegWrite(control_unit_1_regwrite), .ALUorMEM(control_unit_1_aluormem),
    .ALUorLOAD(control_unit_1_aluorload), .ALUorSTORE(control_unit_1_aluorstore),
    .MemWrite(control_unit_1_memwrite), .BEQorBNE(control_unit_1_beqorbne), .BRANCH(control_unit_1_branch),
    .JUMP(and_1_out[1]), .out_5(control_unit_1_out_5));
  Multiplexer #(.width(4), .enable("false")) multiplexer_3 (
    .in0(rom_1_data[3:0]), .in1(rom_1_data[11:8]), .out(multiplexer_3_out), .sel(control_unit_1_aluorstore));
  REGISTER_BANK register_bank_1 (
    .in_1(rom_1_data[7:4]), .in_2(multiplexer_3_out), .WD(multiplexer_5_out), .WE(control_unit_1_regwrite),
    .WRITE_ADDRESS(rom_1_data[11:8]), .out_7(register_bank_1_out_7), .out_8(register_bank_1_out_8),
    .CLOCK(clock_1_out));
  assign bit_extender_3_out = {{12{rom_1_data[3]}}, rom_1_data[3:0]};  // Bit_Extender bit_extender_3
  Multiplexer #(.width(16), .enable("false")) multiplexer_4 (
    .in0(register_bank_1_out_8), .in1(bit_extender_3_out), .out(multiplexer_4_out),
    .sel(control_unit_1_aluormem));
  Multiplexer #(.width(16), .enable("false")) multiplexer_5 (
    .in0(alu_design_1_out_4), .in1(ram_1_data), .out(multiplexer_5_out), .sel(control_unit_1_aluorload));
  ALU_DESIGN alu_design_1 (
    .in_1(register_bank_1_out_7), .in_2(multiplexer_4_out), .out_4(alu_design_1_out_4),
    .in_3(control_unit_1_out_5));
  RAM #(.addrWidth(16), .dataWidth(16), .bus("separate")) ram_1 (
    .addr(alu_design_1_out_4), .din(register_bank_1_out_8), .data(ram_1_data), .str(control_unit_1_memwrite),
    .clk(clock_1_out), .ld(control_unit_1_aluorload));  // open: sel, clr
  or or_1 (or_1_out, alu_design_1_out_4[0], alu_design_1_out_4[1], alu_design_1_out_4[2], alu_design_1_out_4[3], alu_design_1_out_4[4], alu_design_1_out_4[5], alu_design_1_out_4[6], alu_design_1_out_4[7], alu_design_1_out_4[8], alu_design_1_out_4[9], alu_design_1_out_4[10], alu_design_1_out_4[11], alu_design_1_out_4[12], alu_design_1_out_4[13], alu_design_1_out_4[14], alu_design_1_out_4[15]);
  nor nor_1 (nor_1_out, alu_design_1_out_4[0], alu_design_1_out_4[1], alu_design_1_out_4[2], alu_design_1_out_4[3], alu_design_1_out_4[4], alu_design_1_out_4[5], alu_design_1_out_4[6], alu_design_1_out_4[7], alu_design_1_out_4[8], alu_design_1_out_4[9], alu_design_1_out_4[10], alu_design_1_out_4[11], alu_design_1_out_4[12], alu_design_1_out_4[13], alu_design_1_out_4[14], alu_design_1_out_4[15]);

  // Notes on the sheet:
  //   RESET
  //   PC + 1
  //   PROGRAM COUNTER
  //   TARGET + PC+1 
  //   PC + JUMP INDEX
  //   JUMP
  //   INSTRUCTION MEMORY
  //   contents of rom_1 (hex, n*v repeats v):
  //   105
  //   BNE / BEQ
  //   BNE 
  //   BEQ
  //   JUMP INDEX
  //   ALL COMPONENTS COMBINED
  //   BRANCH 
  //   ALU or STORE
  //   OFFSET
  //   DATA WRITE
  //   ALU or MEMORY
  //   ALU or LOAD
  //   BNE
  //   MEMWRITE
  //   BEQ
endmodule

module REGISTER_BANK (
  input  [3:0] in_1,
  input  [3:0] in_2,
  input  [15:0] WD,
  input  WE,
  input  [3:0] WRITE_ADDRESS,
  input  CLOCK,
  output [15:0] out_7,
  output [15:0] out_8
);

  wire and_1_out, and_2_out, and_3_out, and_4_out, and_5_out, and_6_out, and_7_out, and_8_out, and_9_out,
       and_10_out, and_11_out, and_12_out, and_13_out, and_14_out, and_15_out, and_16_out,
       demultiplexer_1_out0, demultiplexer_1_out2, demultiplexer_1_out3, demultiplexer_1_out4,
       demultiplexer_1_out5, demultiplexer_1_out6, demultiplexer_1_out7, demultiplexer_1_out8,
       demultiplexer_1_out9, demultiplexer_1_out10, demultiplexer_1_out11, demultiplexer_1_out12,
       demultiplexer_1_out13, demultiplexer_1_out14, demultiplexer_1_out15, undriven;
  wire [15:0] register_1_q, register_2_q, register_3_q, register_4_q, register_5_q, register_6_q,
       register_7_q, register_8_q, register_9_q, register_10_q, register_11_q, register_12_q, register_13_q,
       register_14_q, register_15_q, register_16_q;

  Demultiplexer #(.select(4), .enable("false")) demultiplexer_1 (
    .out0(demultiplexer_1_out0), .out2(demultiplexer_1_out2), .out3(demultiplexer_1_out3),
    .out4(demultiplexer_1_out4), .out5(demultiplexer_1_out5), .out6(demultiplexer_1_out6),
    .out7(demultiplexer_1_out7), .out8(demultiplexer_1_out8), .out9(demultiplexer_1_out9),
    .out10(demultiplexer_1_out10), .out11(demultiplexer_1_out11), .out12(demultiplexer_1_out12),
    .out13(demultiplexer_1_out13), .out14(demultiplexer_1_out14), .out15(demultiplexer_1_out15), .in(1'b1),
    .sel(WRITE_ADDRESS));  // open: out1
  and and_1 (and_1_out, demultiplexer_1_out0, WE);
  and and_2 (and_2_out, demultiplexer_1_out2, WE);
  and and_3 (and_3_out, demultiplexer_1_out3, WE);
  and and_4 (and_4_out, demultiplexer_1_out4, WE);
  and and_5 (and_5_out, demultiplexer_1_out5, WE);
  and and_6 (and_6_out, demultiplexer_1_out6, WE);
  and and_7 (and_7_out, demultiplexer_1_out7, WE);
  and and_8 (and_8_out, demultiplexer_1_out8, WE);
  and and_9 (and_9_out, demultiplexer_1_out9, WE);
  and and_10 (and_10_out, demultiplexer_1_out10, WE);
  and and_11 (and_11_out, demultiplexer_1_out11, WE);
  and and_12 (and_12_out, demultiplexer_1_out12, WE);
  and and_13 (and_13_out, demultiplexer_1_out13, WE);
  and and_14 (and_14_out, demultiplexer_1_out14, WE);
  and and_15 (and_15_out, demultiplexer_1_out15, WE);
  and and_16 (and_16_out, undriven, WE);
  Register #(.width(16)) register_1 (.D(WD), .en(and_1_out), .Q(register_1_q), .clk(CLOCK));  // open: clr
  Register #(.width(16)) register_2 (.D(WD), .en(and_2_out), .Q(register_2_q), .clk(CLOCK));  // open: clr
  Register #(.width(16)) register_3 (.D(WD), .en(and_3_out), .Q(register_3_q), .clk(CLOCK));  // open: clr
  Register #(.width(16)) register_4 (.D(WD), .en(and_4_out), .Q(register_4_q), .clk(CLOCK));  // open: clr
  Register #(.width(16)) register_5 (.D(WD), .en(and_5_out), .Q(register_5_q), .clk(CLOCK));  // open: clr
  Register #(.width(16)) register_6 (.D(WD), .en(and_6_out), .Q(register_6_q), .clk(CLOCK));  // open: clr
  Register #(.width(16)) register_7 (.D(WD), .en(and_7_out), .Q(register_7_q), .clk(CLOCK));  // open: clr
  Register #(.width(16)) register_8 (.D(WD), .en(and_8_out), .Q(register_8_q), .clk(CLOCK));  // open: clr
  Register #(.width(16)) register_9 (.D(WD), .en(and_9_out), .Q(register_9_q), .clk(CLOCK));  // open: clr
  Register #(.width(16)) register_10 (.D(WD), .en(and_10_out), .Q(register_10_q), .clk(CLOCK));  // open: clr
  Register #(.width(16)) register_11 (.D(WD), .en(and_11_out), .Q(register_11_q), .clk(CLOCK));  // open: clr
  Register #(.width(16)) register_12 (.D(WD), .en(and_12_out), .Q(register_12_q), .clk(CLOCK));  // open: clr
  Register #(.width(16)) register_13 (.en(and_13_out), .Q(register_13_q), .clk(CLOCK));  // open: D, clr
  Register #(.width(16)) register_14 (.D(WD), .en(and_14_out), .Q(register_14_q), .clk(CLOCK));  // open: clr
  Register #(.width(16)) register_15 (.D(WD), .en(and_15_out), .Q(register_15_q), .clk(CLOCK));  // open: clr
  Register #(.width(16)) register_16 (.D(WD), .en(and_16_out), .Q(register_16_q), .clk(CLOCK));  // open: clr
  Multiplexer #(.select(4), .width(16), .enable("false")) multiplexer_1 (
    .in0(register_1_q), .in1(register_2_q), .in2(register_3_q), .in3(register_4_q), .in4(register_5_q),
    .in5(register_6_q), .in6(register_7_q), .in7(register_8_q), .in8(register_9_q), .in9(register_10_q),
    .in10(register_11_q), .in11(register_12_q), .in12(register_13_q), .in13(register_14_q),
    .in14(register_15_q), .in15(register_16_q), .out(out_7), .sel(in_1));
  Multiplexer #(.select(4), .width(16), .enable("false")) multiplexer_2 (
    .in0(register_1_q), .in1(register_2_q), .in2(register_3_q), .in3(register_4_q), .in4(register_5_q),
    .in5(register_6_q), .in6(register_7_q), .in7(register_8_q), .in8(register_9_q), .in9(register_10_q),
    .in10(register_11_q), .in11(register_12_q), .in12(register_13_q), .in13(register_14_q),
    .in14(register_15_q), .in15(register_16_q), .out(out_8), .sel(in_2));

  // Notes on the sheet:
  //   REGISTER FILES
  //   SOURCE REGISTER 1
  //   SOURCE REGISTER 2
endmodule

module ALU_DESIGN (
  input  [15:0] in_1,
  input  [15:0] in_2,
  input  [2:0] in_3,
  output [15:0] out_4
);

  wire [15:0] adder_1_out, and_1_out, not_1_out, or_1_out, subtractor_1_out, xor_1_out;

  Adder #(.width(16)) adder_1 (.a(in_2), .b(in_1), .out(adder_1_out));  // open: cin, cout
  Subtractor #(.width(16)) subtractor_1 (.a(in_2), .b(in_1), .out(subtractor_1_out));  // open: bin, bout
  assign and_1_out = in_2 & in_1;  // AND_Gate and_1, 16 bits wide
  assign or_1_out = in_2 | in_1;  // OR_Gate or_1, 16 bits wide
  assign xor_1_out = in_2 ^ in_1;  // XOR_Gate xor_1, 16 bits wide
  assign not_1_out = ~in_2;  // NOT_Gate not_1, 16 bits wide
  Multiplexer #(.select(3), .width(16)) multiplexer_1 (
    .in0(adder_1_out), .in1(subtractor_1_out), .in2(and_1_out), .in3(or_1_out), .in4(xor_1_out),
    .in5(not_1_out), .out(out_4), .sel(in_3), .en(1'b1));  // open: in6, in7

  // Notes on the sheet:
  //   ALU
  //   ALU SELCT
endmodule

module LOAD_IMPLEMENTATION (
);

  wire button_1_out, clock_1_out, control_unit_1_aluorload, control_unit_1_memwrite, control_unit_1_regwrite;
  wire [2:0] control_unit_1_out_5;
  wire [15:0] adder_1_out, alu_design_1_out_4, bit_extender_1_out, ram_1_data, register_1_q,
       register_bank_1_out_7, rom_1_data;

  Register #(.width(16)) register_1 (
    .D(adder_1_out), .Q(register_1_q), .clk(clock_1_out), .clr(button_1_out));  // open: en
  Button button_1 (.out(button_1_out));
  Adder #(.width(16)) adder_1 (.a(register_1_q), .b(16'h1), .out(adder_1_out));  // open: cin, cout
  ROM #(.addrWidth(16), .dataWidth(16)) rom_1 (.addr(register_1_q), .data(rom_1_data));  // open: sel
  assign bit_extender_1_out = {{12{rom_1_data[3]}}, rom_1_data[3:0]};  // Bit_Extender bit_extender_1
  REGISTER_BANK register_bank_1 (
    .in_1(rom_1_data[7:4]), .WD(ram_1_data), .WE(control_unit_1_regwrite), .WRITE_ADDRESS(rom_1_data[11:8]),
    .out_7(register_bank_1_out_7), .CLOCK(clock_1_out));  // open: in_2, out_8
  Clock clock_1 (.out(clock_1_out));
  CONTROL_UNIT_weef control_unit_weef_1 ();
  CONTROL_UNIT control_unit_1 (
    .OPCODE_15(rom_1_data[12]), .OPCODE_14(rom_1_data[13]), .OPCODE_13(rom_1_data[14]),
    .OPCODE_12(rom_1_data[15]), .RegWrite(control_unit_1_regwrite), .ALUorLOAD(control_unit_1_aluorload),
    .MemWrite(control_unit_1_memwrite), .out_5(control_unit_1_out_5));  // open: ALUorMEM, ALUorSTORE, BEQorBNE, BRANCH, JUMP
  ALU_DESIGN alu_design_1 (
    .in_1(register_bank_1_out_7), .in_2(bit_extender_1_out), .out_4(alu_design_1_out_4),
    .in_3(control_unit_1_out_5));
  RAM #(.addrWidth(16), .dataWidth(16), .bus("separate")) ram_1 (
    .addr(alu_design_1_out_4), .data(ram_1_data), .str(control_unit_1_memwrite), .clk(clock_1_out),
    .ld(control_unit_1_aluorload));  // open: din, sel, clr

  // Notes on the sheet:
  //   PROGRAM COUNTER
  //   RESET
  //   LOAD IMPLEMENTATION
  //   INSTRUCTION MEMORY
  //   contents of rom_1 (hex, n*v repeats v):
  //   884f 72c6
  //   CLOCK
endmodule

module BEQ___BNE (
);

  wire clock_1_out, control_unit_1_beqorbne, control_unit_1_regwrite, multiplexer_2_out, nor_1_out, or_1_out;
  wire [2:0] control_unit_1_out_5;
  wire [15:0] adder_1_out, adder_2_out, alu_design_1_out_4, multiplexer_1_out, register_1_q,
       register_bank_1_out_7, register_bank_1_out_8, rom_1_data, undriven;

  Multiplexer #(.width(16), .enable("false")) multiplexer_1 (
    .in0(adder_1_out), .in1(adder_2_out), .out(multiplexer_1_out), .sel(multiplexer_2_out));
  Register #(.width(16)) register_1 (.D(multiplexer_1_out), .Q(register_1_q), .clk(clock_1_out));  // open: en, clr
  Adder #(.width(16)) adder_1 (.a(register_1_q), .b(16'h1), .out(adder_1_out));  // open: cin, cout
  ROM #(.addrWidth(16), .dataWidth(16)) rom_1 (.addr(register_1_q), .data(rom_1_data));  // open: sel
  Adder #(.width(16)) adder_2 (.a(undriven), .b(adder_1_out), .out(adder_2_out));  // open: cin, cout
  Bit_Extender #(.in_width(16), .out_width(4), .\type ("sign")) bit_extender_1 (.in(undriven), .out(rom_1_data[3:0]));
  Clock clock_1 (.out(clock_1_out));
  REGISTER_BANK register_bank_1 (
    .in_1(rom_1_data[7:4]), .in_2(rom_1_data[11:8]), .WE(control_unit_1_regwrite),
    .out_7(register_bank_1_out_7), .out_8(register_bank_1_out_8), .CLOCK(clock_1_out));  // open: WD, WRITE_ADDRESS
  Multiplexer #(.enable("false")) multiplexer_2 (
    .in0(or_1_out), .in1(nor_1_out), .out(multiplexer_2_out), .sel(control_unit_1_beqorbne));
  CONTROL_UNIT control_unit_1 (
    .OPCODE_15(rom_1_data[12]), .OPCODE_14(rom_1_data[13]), .OPCODE_13(rom_1_data[14]),
    .OPCODE_12(rom_1_data[15]), .RegWrite(control_unit_1_regwrite), .BEQorBNE(control_unit_1_beqorbne),
    .out_5(control_unit_1_out_5));  // open: ALUorMEM, ALUorLOAD, ALUorSTORE, MemWrite, BRANCH, JUMP
  ALU_DESIGN alu_design_1 (
    .in_1(register_bank_1_out_7), .in_2(register_bank_1_out_8), .out_4(alu_design_1_out_4),
    .in_3(control_unit_1_out_5));
  or or_1 (or_1_out, alu_design_1_out_4[0], alu_design_1_out_4[1], alu_design_1_out_4[2], alu_design_1_out_4[3], alu_design_1_out_4[4], alu_design_1_out_4[5], alu_design_1_out_4[6], alu_design_1_out_4[7], alu_design_1_out_4[8], alu_design_1_out_4[9], alu_design_1_out_4[10], alu_design_1_out_4[11], alu_design_1_out_4[12], alu_design_1_out_4[13], alu_design_1_out_4[14], alu_design_1_out_4[15]);
  nor nor_1 (nor_1_out, alu_design_1_out_4[0], alu_design_1_out_4[1], alu_design_1_out_4[2], alu_design_1_out_4[3], alu_design_1_out_4[4], alu_design_1_out_4[5], alu_design_1_out_4[6], alu_design_1_out_4[7], alu_design_1_out_4[8], alu_design_1_out_4[9], alu_design_1_out_4[10], alu_design_1_out_4[11], alu_design_1_out_4[12], alu_design_1_out_4[13], alu_design_1_out_4[14], alu_design_1_out_4[15]);

  // Notes on the sheet:
  //   PC + 1
  //   BNE / BEQ IMPLEMENTATION
  //   TARGET + PC+1 
  //   contents of rom_1 (hex, n*v repeats v):
  //   884f 72c6
  //   BNE / BEQ
  //   BNE
  //   BEQ
endmodule

module JUMP (
);

  wire button_1_out, clock_1_out;
  wire [11:0] bit_extender_1_out;
  wire [15:0] adder_1_out, register_1_q, undriven;
  wire [15:12] rom_1_data;

  Button button_1 (.out(button_1_out));
  Register #(.width(16)) register_1 (
    .D(adder_1_out), .Q(register_1_q), .clk(clock_1_out), .clr(button_1_out));  // open: en
  Clock clock_1 (.out(clock_1_out));
  Bit_Extender #(.in_width(16), .out_width(12), .\type ("sign")) bit_extender_1 (
    .in(undriven), .out(bit_extender_1_out));
  ROM #(.addrWidth(16), .dataWidth(16)) rom_1 (
    .addr(register_1_q), .data({rom_1_data, bit_extender_1_out}));  // open: sel
  Adder #(.width(16)) adder_1 (.a(undriven), .b(register_1_q), .out(adder_1_out));  // open: cin, cout
  CONTROL_UNIT control_unit_1 (
    .OPCODE_15(rom_1_data[12]), .OPCODE_14(rom_1_data[13]), .OPCODE_13(rom_1_data[14]),
    .OPCODE_12(rom_1_data[15]));  // open: RegWrite, ALUorMEM, ALUorLOAD, ALUorSTORE, MemWrite, BEQorBNE, BRANCH, JUMP, out_5

  // Notes on the sheet:
  //   PROGRAM COUNTER
  //   RESET
  //   JUMP IMPLEMENTATION
  //   INSTRUCTION MEMORY
  //   contents of rom_1 (hex, n*v repeats v):
  //   884f 72c6
endmodule

module CONTROL_UNIT (
  input  OPCODE_15,
  input  OPCODE_14,
  input  OPCODE_13,
  input  OPCODE_12,
  output [2:0] out_5,
  output RegWrite,
  output ALUorMEM,
  output ALUorLOAD,
  output ALUorSTORE,
  output MemWrite,
  output BEQorBNE,
  output BRANCH,
  output JUMP
);

  wire and_1_out, and_2_out, and_3_out, and_5_out, and_8_out, and_9_out, and_10_out, and_11_out, and_12_out,
       and_13_out, and_14_out, and_15_out, and_16_out, not_1_out, not_2_out, not_3_out, not_4_out, not_5_out,
       not_6_out, not_7_out, not_8_out, not_9_out, not_10_out, not_11_out, not_12_out, not_13_out,
       not_14_out, not_16_out, not_17_out, not_18_out;

  not not_1 (not_1_out, OPCODE_15);
  not not_2 (not_2_out, OPCODE_13);
  not not_3 (not_3_out, OPCODE_15);
  not not_4 (not_4_out, OPCODE_14);
  not not_5 (not_5_out, OPCODE_15);
  not not_6 (not_6_out, OPCODE_14);
  not not_7 (not_7_out, OPCODE_13);
  not not_8 (not_8_out, OPCODE_13);
  not not_9 (not_9_out, OPCODE_15);
  not not_10 (not_10_out, OPCODE_14);
  not not_11 (not_11_out, OPCODE_15);
  not not_12 (not_12_out, OPCODE_12);
  not not_13 (not_13_out, OPCODE_14);
  not not_14 (not_14_out, OPCODE_13);
  and and_1 (and_1_out, OPCODE_14, OPCODE_13);
  and and_2 (and_2_out, OPCODE_15, OPCODE_13);
  and and_3 (and_3_out, OPCODE_15, OPCODE_14);
  and and_4 (ALUorLOAD, OPCODE_14, OPCODE_13);
  and and_5 (and_5_out, OPCODE_14, OPCODE_13);
  and and_6 (MemWrite, OPCODE_14, OPCODE_13, OPCODE_12);
  not not_15 (BEQorBNE, OPCODE_12);
  not not_16 (not_16_out, OPCODE_14);
  not not_17 (not_17_out, OPCODE_13);
  not not_18 (not_18_out, OPCODE_12);
  and and_7 (out_5[2], not_1_out, OPCODE_14, not_2_out);
  and and_8 (and_8_out, not_3_out, not_4_out, OPCODE_13);
  and and_9 (and_9_out, OPCODE_15, OPCODE_14, OPCODE_12);
  and and_10 (and_10_out, not_5_out, not_6_out, OPCODE_12);
  and and_11 (and_11_out, not_7_out, OPCODE_12);
  and and_12 (and_12_out, OPCODE_15, not_8_out);
  and and_13 (and_13_out, not_9_out, not_10_out);
  and and_14 (and_14_out, not_11_out, not_12_out);
  and and_15 (and_15_out, not_13_out, OPCODE_13, OPCODE_12);
  and and_16 (and_16_out, OPCODE_14, not_14_out);
  or or_1 (ALUorMEM, and_1_out, and_2_out, and_3_out);
  or or_2 (ALUorSTORE, and_5_out, OPCODE_15);
  and and_17 (BRANCH, OPCODE_15, not_16_out, not_17_out);
  and and_18 (JUMP, OPCODE_15, OPCODE_13, not_18_out);
  or or_3 (out_5[1], and_8_out, and_9_out);
  or or_4 (out_5[0], and_10_out, and_11_out, and_12_out);
  or or_5 (RegWrite, and_13_out, and_14_out, and_15_out, and_16_out);

  // Notes on the sheet:
  //   CONTROL UNIT
endmodule

module ALU_IMPLEMENTATION (
);

  wire button_1_out, clock_1_out, control_unit_1_regwrite;
  wire [2:0] control_unit_1_out_5;
  wire [15:0] adder_1_out, alu_design_1_out_4, register_1_q, register_bank_1_out_7, register_bank_1_out_8,
       rom_1_data;

  Register #(.width(16)) register_1 (
    .D(adder_1_out), .Q(register_1_q), .clk(clock_1_out), .clr(button_1_out));  // open: en
  Button button_1 (.out(button_1_out));
  Adder #(.width(16)) adder_1 (.a(register_1_q), .b(16'h1), .out(adder_1_out));  // open: cin, cout
  ROM #(.addrWidth(16), .dataWidth(16)) rom_1 (.addr(register_1_q), .data(rom_1_data));  // open: sel
  REGISTER_BANK register_bank_1 (
    .in_1(rom_1_data[7:4]), .in_2(rom_1_data[3:0]), .WD(alu_design_1_out_4), .WE(control_unit_1_regwrite),
    .WRITE_ADDRESS(rom_1_data[11:8]), .out_7(register_bank_1_out_7), .out_8(register_bank_1_out_8),
    .CLOCK(clock_1_out));
  Clock clock_1 (.out(clock_1_out));
  CONTROL_UNIT control_unit_1 (
    .OPCODE_15(rom_1_data[12]), .OPCODE_14(rom_1_data[13]), .OPCODE_13(rom_1_data[14]),
    .OPCODE_12(rom_1_data[15]), .RegWrite(control_unit_1_regwrite), .out_5(control_unit_1_out_5));  // open: ALUorMEM, ALUorLOAD, ALUorSTORE, MemWrite, BEQorBNE, BRANCH, JUMP
  ALU_DESIGN alu_design_1 (
    .in_1(register_bank_1_out_7), .in_2(register_bank_1_out_8), .out_4(alu_design_1_out_4),
    .in_3(control_unit_1_out_5));

  // Notes on the sheet:
  //   RESET
  //   PROGRAM COUNTER
  //   ALU IMPLEMENTATION
  //   INSTRUCTION MEMORY
  //   contents of rom_1 (hex, n*v repeats v):
  //   884f 72c6
  //   CLOCK
endmodule

module ALU_IMMEDIATE (
);

  wire button_1_out, clock_1_out, control_unit_1_regwrite;
  wire [2:0] control_unit_1_out_5;
  wire [15:0] adder_1_out, alu_design_1_out_4, bit_extender_1_out, register_1_q, register_bank_1_out_7,
       rom_1_data;

  Register #(.width(16)) register_1 (
    .D(adder_1_out), .Q(register_1_q), .clk(clock_1_out), .clr(button_1_out));  // open: en
  Button button_1 (.out(button_1_out));
  Adder #(.width(16)) adder_1 (.a(register_1_q), .b(16'h1), .out(adder_1_out));  // open: cin, cout
  ROM #(.addrWidth(16), .dataWidth(16)) rom_1 (.addr(register_1_q), .data(rom_1_data));  // open: sel
  assign bit_extender_1_out = {{12{rom_1_data[3]}}, rom_1_data[3:0]};  // Bit_Extender bit_extender_1
  REGISTER_BANK register_bank_1 (
    .in_1(rom_1_data[7:4]), .WD(alu_design_1_out_4), .WE(control_unit_1_regwrite),
    .WRITE_ADDRESS(rom_1_data[11:8]), .out_7(register_bank_1_out_7), .CLOCK(clock_1_out));  // open: in_2, out_8
  Clock clock_1 (.out(clock_1_out));
  CONTROL_UNIT control_unit_1 (
    .OPCODE_15(rom_1_data[12]), .OPCODE_14(rom_1_data[13]), .OPCODE_13(rom_1_data[14]),
    .OPCODE_12(rom_1_data[15]), .RegWrite(control_unit_1_regwrite), .out_5(control_unit_1_out_5));  // open: ALUorMEM, ALUorLOAD, ALUorSTORE, MemWrite, BEQorBNE, BRANCH, JUMP
  ALU_DESIGN alu_design_1 (
    .in_1(register_bank_1_out_7), .in_2(bit_extender_1_out), .out_4(alu_design_1_out_4),
    .in_3(control_unit_1_out_5));

  // Notes on the sheet:
  //   RESET
  //   PROGRAM COUNTER
  //   ALU IMMEDIATE
  //   INSTRUCTION MEMORY
  //   contents of rom_1 (hex, n*v repeats v):
  //   884f 72c6
  //   CLOCK
endmodule

module STORE_IMPLEMENTATION (
);

  wire button_1_out, clock_1_out, control_unit_1_aluorload, control_unit_1_memwrite, control_unit_1_regwrite;
  wire [2:0] control_unit_1_out_5;
  wire [15:0] adder_1_out, alu_design_1_out_4, bit_extender_1_out, ram_1_data, register_1_q,
       register_bank_1_out_7, register_bank_1_out_8, rom_1_data;

  Register #(.width(16)) register_1 (
    .D(adder_1_out), .Q(register_1_q), .clk(clock_1_out), .clr(button_1_out));  // open: en
  Button button_1 (.out(button_1_out));
  Adder #(.width(16)) adder_1 (.a(register_1_q), .b(16'h1), .out(adder_1_out));  // open: cin, cout
  ROM #(.addrWidth(16), .dataWidth(16)) rom_1 (.addr(register_1_q), .data(rom_1_data));  // open: sel
  assign bit_extender_1_out = {{12{rom_1_data[3]}}, rom_1_data[3:0]};  // Bit_Extender bit_extender_1
  REGISTER_BANK register_bank_1 (
    .in_1(rom_1_data[7:4]), .in_2(rom_1_data[11:8]), .WD(ram_1_data), .WE(control_unit_1_regwrite),
    .out_7(register_bank_1_out_7), .out_8(register_bank_1_out_8), .CLOCK(clock_1_out));  // open: WRITE_ADDRESS
  Clock clock_1 (.out(clock_1_out));
  CONTROL_UNIT_weef control_unit_weef_1 ();
  CONTROL_UNIT control_unit_1 (
    .OPCODE_15(rom_1_data[12]), .OPCODE_14(rom_1_data[13]), .OPCODE_13(rom_1_data[14]),
    .OPCODE_12(rom_1_data[15]), .RegWrite(control_unit_1_regwrite), .ALUorLOAD(control_unit_1_aluorload),
    .MemWrite(control_unit_1_memwrite), .out_5(control_unit_1_out_5));  // open: ALUorMEM, ALUorSTORE, BEQorBNE, BRANCH, JUMP
  ALU_DESIGN alu_design_1 (
    .in_1(register_bank_1_out_7), .in_2(bit_extender_1_out), .out_4(alu_design_1_out_4),
    .in_3(control_unit_1_out_5));
  RAM #(.addrWidth(16), .dataWidth(16), .bus("separate")) ram_1 (
    .addr(alu_design_1_out_4), .din(register_bank_1_out_8), .data(ram_1_data), .str(control_unit_1_memwrite),
    .clk(clock_1_out), .ld(control_unit_1_aluorload));  // open: sel, clr

  // Notes on the sheet:
  //   PROGRAM COUNTER
  //   RESET
  //   STORE IMPLEMENTATION
  //   INSTRUCTION MEMORY
  //   contents of rom_1 (hex, n*v repeats v):
  //   884f 72c6
  //   CLOCK
endmodule
